// Logisim project EP1 - Breno Nogueira.circ as structural Verilog: 2 circuits, main circuit main
module main (
);

  wire and_1_out, and_2_out, and_3_out, and_4_out, and_5_out, and_6_out, and_7_out, and_8_out, and_9_out,
       and_10_out, and_11_out, and_12_out, and_13_out, and_14_out, and_15_out, and_16_out, and_17_out,
       and_18_out, and_19_out, and_20_out, and_21_out, and_22_out, and_23_out, and_24_out, and_25_out,
       and_26_out, and_27_out, and_28_out, and_29_out, and_30_out, and_31_out, and_32_out, and_33_out,
       and_34_out, and_35_out, not_1_out, not_2_out, not_3_out, or_1_out, or_2_out, or_3_out, or_4_out,
       or_5_out, or_6_out, or_7_out, or_8_out, or_9_out, or_10_out, or_11_out, or_12_out, or_13_out,
       or_14_out, or_15_out, or_16_out, xor_1_out, xor_2_out, xor_3_out, xor_4_out, xor_5_out, xor_6_out,
       xor_7_out, xor_8_out, xor_9_out, xor_11_out, xor_13_out, xor_15_out, xor_17_out, xor_19_out,
       xor_21_out, xor_23_out, xor_26_out, xor_27_out, xor_28_out, xor_29_out, xor_30_out, xor_31_out,
       xor_34_out, xor_36_out, xor_38_out, xor_40_out, xor_41_out, xor_44_out;
  wire [3:0] xor_10_out, xor_12_out, xor_25_out, xor_32_out, xor_33_out;

  Hex_Digit_Display hex_digit_display_1 (.value(xor_33_out));  // open: dp
  LED led_1 (.in(xor_33_out[2]));
  LED led_2 (.in(xor_33_out[3]));
  LED led_3 (.in(xor_33_out[1]));
  LED led_4 (.in(xor_33_out[0]));
  LED led_5 (.in(xor_33_out[3]));
  Hex_Digit_Display hex_digit_display_2 (.value({1'b0, xor_33_out[2:0]}));  // open: dp
  LED led_6 (.in(1'b1));
  Hex_Digit_Display hex_digit_display_3 (.value(4'b0110));  // open: dp
  LED led_7 (.in(1'b0));
  Hex_Digit_Display hex_digit_display_4 (.value(4'b0010));  // open: dp
  and and_1 (and_1_out, 1'b1, 1'b1);
  not not_1 (not_1_out, 1'b1);
  and and_2 (and_2_out, 1'b0, 1'b1);
  xor xor_1 (xor_1_out, and_1_out, 1'b0);
  xor xor_2 (xor_2_out, and_1_out, 1'b1);
  xor xor_3 (xor_3_out, and_1_out, 1'b1);
  xor xor_4 (xor_4_out, and_1_out, not_1_out);
  not not_2 (not_2_out, 1'b1);
  xor xor_5 (xor_5_out, and_2_out, 1'b0);
  xor xor_6 (xor_6_out, and_2_out, 1'b1);
  xor xor_7 (xor_7_out, and_2_out, 1'b0);
  xor xor_8 (xor_8_out, and_2_out, not_2_out);
  and and_3 (and_3_out, 1'b1, xor_1_out);
  xor xor_9 (xor_9_out, xor_1_out, 1'b1);
  xor xor_10 (xor_10_out[0], xor_9_out, 1'b0);
  and and_4 (and_4_out, 1'b0, xor_9_out);
  and and_5 (and_5_out, 1'b0, xor_5_out);
  xor xor_11 (xor_11_out, xor_5_out, 1'b0);
  xor xor_12 (xor_12_out[0], xor_11_out, 1'b0);
  and and_6 (and_6_out, 1'b0, xor_11_out);
  or or_1 (or_1_out, and_3_out, and_4_out);
  or or_2 (or_2_out, and_5_out, and_6_out);
  and and_7 (and_7_out, 1'b0, xor_2_out);
  xor xor_13 (xor_13_out, xor_2_out, 1'b0);
  xor xor_14 (xor_10_out[1], xor_13_out, or_1_out);
  and and_8 (and_8_out, or_1_out, xor_13_out);
  and and_9 (and_9_out, 1'b0, xor_6_out);
  xor xor_15 (xor_15_out, xor_6_out, 1'b0);
  xor xor_16 (xor_12_out[1], xor_15_out, or_2_out);
  and and_10 (and_10_out, or_2_out, xor_15_out);
  or or_3 (or_3_out, and_7_out, and_8_out);
  or or_4 (or_4_out, and_9_out, and_10_out);
  and and_11 (and_11_out, 1'b0, xor_3_out);
  xor xor_17 (xor_17_out, xor_3_out, 1'b0);
  xor xor_18 (xor_10_out[2], xor_17_out, or_3_out);
  and and_12 (and_12_out, or_3_out, xor_17_out);
  and and_13 (and_13_out, 1'b0, xor_7_out);
  xor xor_19 (xor_19_out, xor_7_out, 1'b0);
  or or_5 (or_5_out, and_11_out, and_12_out);
  xor xor_20 (xor_12_out[2], xor_19_out, or_4_out);
  and and_14 (and_14_out, or_4_out, xor_19_out);
  or or_6 (or_6_out, and_13_out, and_14_out);
  and and_15 (and_15_out, 1'b0, xor_4_out);
  xor xor_21 (xor_21_out, xor_4_out, 1'b0);
  xor xor_22 (xor_10_out[3], xor_21_out, or_5_out);
  and and_16 (and_16_out, or_5_out, xor_21_out);
  and and_17 (and_17_out, 1'b0, xor_8_out);
  xor xor_23 (xor_23_out, xor_8_out, 1'b0);
  or or_7 (or_7_out, and_15_out, and_16_out);
  xor xor_24 (xor_12_out[3], xor_23_out, or_6_out);
  and and_18 (and_18_out, or_6_out, xor_23_out);
  LED led_8 (.in(or_7_out));
  Hex_Digit_Display hex_digit_display_5 (.value(xor_32_out));  // open: dp
  or or_8 (or_8_out, and_17_out, and_18_out);
  LED led_9 (.in(xor_32_out[3]));
  LED led_10 (.in(xor_32_out[2]));
  LED led_11 (.in(or_8_out));
  LED led_12 (.in(xor_32_out[1]));
  LED led_13 (.in(xor_32_out[0]));
  assign xor_25_out = 4'b0000 ^ xor_12_out;  // XOR_Gate xor_25, 4 bits wide
  and and_19 (and_19_out, xor_32_out[3], 1'b1);
  not not_3 (not_3_out, 1'b1);
  xor xor_26 (xor_26_out, and_19_out, xor_32_out[0]);
  xor xor_27 (xor_27_out, and_19_out, xor_32_out[1]);
  xor xor_28 (xor_28_out, and_19_out, xor_32_out[2]);
  xor xor_29 (xor_29_out, and_19_out, not_3_out);
  xor xor_30 (xor_30_out, xor_10_out[0], xor_25_out[0]);
  and and_20 (and_20_out, xor_32_out[3], xor_26_out);
  xor xor_31 (xor_31_out, xor_26_out, xor_32_out[3]);
  and and_21 (and_21_out, xor_25_out[0], xor_10_out[0]);
  xor xor_32 (xor_32_out[0], xor_30_out, 1'b0);
  and and_22 (and_22_out, 1'b0, xor_30_out);
  xor xor_33 (xor_33_out[0], xor_31_out, 1'b0);
  and and_23 (and_23_out, 1'b0, xor_31_out);
  or or_9 (or_9_out, and_21_out, and_22_out);
  or or_10 (or_10_out, and_20_out, and_23_out);
  and and_24 (and_24_out, 1'b0, xor_27_out);
  xor xor_34 (xor_34_out, xor_27_out, 1'b0);
  xor xor_35 (xor_33_out[1], xor_34_out, or_10_out);
  and and_25 (and_25_out, or_10_out, xor_34_out);
  xor xor_36 (xor_36_out, xor_10_out[1], xor_25_out[1]);
  xor xor_37 (xor_32_out[1], xor_36_out, or_9_out);
  and and_26 (and_26_out, or_9_out, xor_36_out);
  or or_11 (or_11_out, and_24_out, and_25_out);
  and and_27 (and_27_out, xor_25_out[1], xor_10_out[1]);
  and and_28 (and_28_out, 1'b0, xor_28_out);
  xor xor_38 (xor_38_out, xor_28_out, 1'b0);
  or or_12 (or_12_out, and_27_out, and_26_out);
  xor xor_39 (xor_33_out[2], xor_38_out, or_11_out);
  and and_29 (and_29_out, or_11_out, xor_38_out);
  or or_13 (or_13_out, and_28_out, and_29_out);
  and and_30 (and_30_out, 1'b0, xor_29_out);
  xor xor_40 (xor_40_out, xor_29_out, 1'b0);
  xor xor_41 (xor_41_out, xor_10_out[2], xor_25_out[2]);
  xor xor_42 (xor_33_out[3], xor_40_out, or_13_out);
  and and_31 (and_31_out, or_13_out, xor_40_out);
  and and_32 (and_32_out, or_12_out, xor_41_out);
  or or_14 (or_14_out, and_30_out, and_31_out);
  and and_33 (and_33_out, xor_25_out[2], xor_10_out[2]);
  xor xor_43 (xor_32_out[2], xor_41_out, or_12_out);
  LED led_14 (.in(or_14_out));
  or or_15 (or_15_out, and_33_out, and_32_out);
  xor xor_44 (xor_44_out, xor_10_out[3], xor_25_out[3]);
  and and_34 (and_34_out, xor_25_out[3], xor_10_out[3]);
  xor xor_45 (xor_32_out[3], xor_44_out, or_15_out);
  and and_35 (and_35_out, or_15_out, xor_44_out);
  or or_16 (or_16_out, and_34_out, and_35_out);
  LED led_15 (.in(or_16_out));

  // Notes on the sheet:
  //   resultado = A {+,-} B
  //   Operando A
  //   —
  //   4
  //   2
  //   1
  //   0:soma; 1: subtrai
  //   Operando B
  //   —
  //   4
  //   1
  //   2
  //   Se esta entrada = 1 então complementa
  //   Se esta entrada = 1 então complementa
  //   Para converter o número negativo, tem que ser 0
  //   Para converter o número negativo, tem que ser 0
  //   Se esta entrada = 0 adiciona, então sempre 0
  //   Se esta entrada = 0 adiciona, então sempre 0
  //   Adiciona 1
  //   Adiciona 1
  //   Número em Complemento de 2
  //   Complementa
  //   Adiciona 1
endmodule

module Conversor (
);

  wire and_1_out, and_2_out, and_3_out, and_4_out, and_5_out, and_6_out, and_7_out, and_8_out, and_9_out,
       not_1_out, not_2_out, or_1_out, or_2_out, or_3_out, or_4_out, xor_1_out, xor_2_out, xor_3_out,
       xor_4_out, xor_5_out, xor_6_out, xor_7_out, xor_8_out, xor_9_out, xor_10_out, xor_11_out, xor_12_out;
  wire [3:0] bit_extender_1_out;

  LED led_1 (.in(1'b0));
  Hex_Digit_Display hex_digit_display_1 (.value(4'b0101));  // open: dp
  not not_1 (not_1_out, not_2_out);
  and and_1 (and_1_out, 1'b0, 1'b1);
  not not_2 (not_2_out, 1'b1);
  assign bit_extender_1_out = {{3{1'b0}}, not_1_out};  // Bit_Extender bit_extender_1
  xor xor_1 (xor_1_out, and_1_out, 1'b1);
  xor xor_2 (xor_2_out, and_1_out, 1'b0);
  xor xor_3 (xor_3_out, and_1_out, 1'b1);
  xor xor_4 (xor_4_out, and_1_out, not_2_out);
  and and_2 (and_2_out, bit_extender_1_out[0], xor_1_out);
  xor xor_5 (xor_5_out, xor_1_out, bit_extender_1_out[0]);
  xor xor_6 (xor_6_out, xor_5_out, 1'b0);
  and and_3 (and_3_out, 1'b0, xor_5_out);
  or or_1 (or_1_out, and_2_out, and_3_out);
  and and_4 (and_4_out, bit_extender_1_out[1], xor_2_out);
  xor xor_7 (xor_7_out, xor_2_out, bit_extender_1_out[1]);
  and and_5 (and_5_out, or_1_out, xor_7_out);
  xor xor_8 (xor_8_out, xor_7_out, or_1_out);
  or or_2 (or_2_out, and_4_out, and_5_out);
  and and_6 (and_6_out, bit_extender_1_out[2], xor_3_out);
  xor xor_9 (xor_9_out, xor_3_out, bit_extender_1_out[2]);
  xor xor_10 (xor_10_out, xor_9_out, or_2_out);
  and and_7 (and_7_out, or_2_out, xor_9_out);
  or or_3 (or_3_out, and_6_out, and_7_out);
  and and_8 (and_8_out, bit_extender_1_out[3], xor_4_out);
  xor xor_11 (xor_11_out, xor_4_out, bit_extender_1_out[3]);
  xor xor_12 (xor_12_out, xor_11_out, or_3_out);
  and and_9 (and_9_out, or_3_out, xor_11_out);
  or or_4 (or_4_out, and_8_out, and_9_out);
  LED led_2 (.in(or_4_out));

  // Notes on the sheet:
  //   Se esta entrada = 1 então complementa
  //   Para converter o número negativo, tem que ser 0
  //   Se esta entrada = 0 adiciona, então sempre 0
endmodule
