// Logisim project Tarefinha 2 - Breno Nogueira.circ as structural Verilog: 1 circuit, main circuit main
module main (
);

  wire and_1_out, and_2_out, and_3_out, and_4_out, and_5_out, and_6_out, and_7_out, and_8_out, or_1_out,
       or_2_out, or_3_out, or_4_out, xor_2_out, xor_4_out, xor_6_out, xor_8_out;
  wire [3:0] xor_1_out, xor_3_out;

  Hex_Digit_Display hex_digit_display_1 (.value(xor_3_out));  // open: dp
  Hex_Digit_Display hex_digit_display_2 (.value(4'b1011));  // open: dp
  Hex_Digit_Display hex_digit_display_3 (.value(4'b1010));  // open: dp
  LED led_1 (.in(xor_3_out[3]));
  LED led_2 (.in(xor_3_out[2]));
  LED led_3 (.in(xor_3_out[1]));
  assign xor_1_out = 4'b1111 ^ 4'b1011;  // XOR_Gate xor_1, 4 bits wide
  LED led_4 (.in(xor_3_out[0]));
  LED led_5 (.in(xor_3_out[3]));
  Hex_Digit_Display hex_digit_display_4 (.value({1'b0, xor_3_out[2:0]}));  // open: dp
  xor xor_2 (xor_2_out, 1'b0, xor_1_out[0]);
  xor xor_3 (xor_3_out[0], xor_2_out, 1'b1);
  and and_1 (and_1_out, 1'b1, xor_2_out);
  and and_2 (and_2_out, xor_1_out[0], 1'b0);
  or or_1 (or_1_out, and_2_out, and_1_out);
  xor xor_4 (xor_4_out, 1'b1, xor_1_out[1]);
  and and_3 (and_3_out, xor_1_out[1], 1'b1);
  xor xor_5 (xor_3_out[1], xor_4_out, or_1_out);
  and and_4 (and_4_out, or_1_out, xor_4_out);
  or or_2 (or_2_out, and_3_out, and_4_out);
  xor xor_6 (xor_6_out, 1'b0, xor_1_out[2]);
  and and_5 (and_5_out, xor_1_out[2], 1'b0);
  xor xor_7 (xor_3_out[2], xor_6_out, or_2_out);
  and and_6 (and_6_out, or_2_out, xor_6_out);
  or or_3 (or_3_out, and_5_out, and_6_out);
  xor xor_8 (xor_8_out, 1'b1, xor_1_out[3]);
  and and_7 (and_7_out, or_3_out, xor_8_out);
  and and_8 (and_8_out, xor_1_out[3], 1'b1);
  xor xor_9 (xor_3_out[3], xor_8_out, or_3_out);
  LED led_6 (.in(or_4_out));
  or or_4 (or_4_out, and_8_out, and_7_out);

  // Notes on the sheet:
  //   operando B
  //   operando A
  //   resultado = A {+,-} B
  //   resultado
  //   0:soma; 1: subtrai
endmodule
