// Logisim project somador-subtrator.circ as structural Verilog: 1 circuit, main circuit main
module main (
);

  wire adder_1_cout;
  wire [2:0] adder_1_out;
  wire [3:0] xor_1_out;
  wire [3:3] adder_1_out_2;

  Hex_Digit_Display hex_digit_display_1 (.value(4'b0111));  // open: dp
  Hex_Digit_Display hex_digit_display_2 (.value(4'b0100));  // open: dp
  assign xor_1_out = 4'b1111 ^ 4'b0111;  // XOR_Gate xor_1, 4 bits wide
  Adder #(.width(4)) adder_1 (
    .a(xor_1_out), .b(4'b0100), .out({adder_1_out_2[3], adder_1_out}), .cin(1'b1), .cout(adder_1_cout));
  LED led_1 (.in(adder_1_cout));
  Hex_Digit_Display hex_digit_display_3 (.value({adder_1_out_2[3], adder_1_out}));  // open: dp
  LED led_2 (.in(adder_1_out[2]));
  LED led_3 (.in(adder_1_out_2[3]));
  LED led_4 (.in(adder_1_out[0]));
  LED led_5 (.in(adder_1_out[1]));
  LED led_6 (.in(adder_1_out_2[3]));
  // AND_Gate and_1 is placed but not wired
  // AND_Gate and_2 is placed but not wired
  // AND_Gate and_3 is placed but not wired
  Hex_Digit_Display hex_digit_display_4 (.value({1'b0, adder_1_out}));  // open: dp

  // Notes on the sheet:
  //   operando B
  //   operando A
  //   resultado = A {+,-} B
  //   0:soma; 1: subtrai
  //   resultado
endmodule
